// Digital circuit Example-Circuit.dig as structural Verilog
module Example_Circuit (
  input  B,
  input  C,
  input  A,
  output ABC_plus_A_BC
);

  wire and_1_out, not_1_out, or_1_out;

  and and_1 (and_1_out, B, C);
  not not_1 (not_1_out, A);
  or or_1 (or_1_out, not_1_out, A);
  and and_2 (ABC_plus_A_BC, and_1_out, or_1_out);
  LED led_1 (.in(ABC_plus_A_BC));
endmodule
